# Fritzing sketch Untitled Sketch (saved by Fritzing 0.7.7b)
breadboards: 1

parts:
  Arduino1 = Arduino
  R1 = Resistor [tolerance=±5% resistance=10k package=THT]
  R2 = Resistor [tolerance=±5% resistance=220 package=THT]
  R3 = Resistor [tolerance=±5% resistance=220 package=THT]
  LED1 = LED - 5mm [color="Red (633nm)" package="5 mm [THT]"]
  LED2 = LED - 5mm [color="Yellow (574nm)" package="5 mm [THT]"]
  S1 = Pushbutton [package="[THT]"]
  R4 = Resistor [tolerance=±5% resistance=10k package=THT]
  S2 = Pushbutton [package="[THT]"]

nets (from the schematic view):
  N1: Arduino1.GND, LED1.cathode, LED2.cathode, S1.Pin_1, S1.Pin_2, S2.Pin_3, S2.Pin_4
  N2: Arduino1.D9, R3.Pin_0
  N3: Arduino1.D8, R2.Pin_0
  N4: Arduino1.D7, R1.Pin_1, S1.Pin_3, S1.Pin_4
  N5: Arduino1.D6, R4.Pin_0, S2.Pin_1, S2.Pin_2
  N6: Arduino1.+5V, R1.Pin_0, R4.Pin_1
  N7: R2.Pin_1, LED2.anode
  N8: R3.Pin_1, LED1.anode

// code stored in the sketch: Pressure_Tester.ino
#define RLED 9
#define YLED 8
#define Pressure 7
#define Reset 6

boolean State=1;
boolean PBState=1;
boolean RBState=1;
boolean StateSave=1;

void setup()
{
  pinMode(RLED,OUTPUT);
  pinMode(YLED,OUTPUT);
  pinMode(Pressure,INPUT);
  pinMode(Reset,INPUT);
}

void loop()
{
  PBState=digitalRead(Pressure);
  RBState=digitalRead(Reset);
  if(PBState==LOW)
  {
    digitalWrite(RLED,HIGH);
    digitalWrite(YLED,HIGH);
    StateSave = LOW;
  }
  if(PBState==HIGH&&StateSave==LOW&&RBState==HIGH)
  {
    digitalWrite(RLED,LOW);
    digitalWrite(YLED,HIGH);
  }
  if(RBState==LOW)
  {
    digitalWrite(RLED,LOW);
    digitalWrite(YLED,LOW);
    StateSave = HIGH;
  }
}
