# Fritzing sketch SwitchCaseStatment (saved by Fritzing 0.7.7b)
breadboards: 1

parts:
  Arduino1 = Arduino
  S1 = Pushbutton [package="[THT]"]
  R1 = Resistor [tolerance=±5% resistance=10k package=THT]
  LED1 = LED - 5mm [color="Yellow (595nm)" package="5 mm [THT]"]
  LED2 = LED - 5mm [color="Red (633nm)" package="5 mm [THT]"]
  LED3 = LED - 5mm [color="Green (565nm)" package="5 mm [THT]"]
  R2 = Resistor [tolerance=±5% resistance=470 package=THT]
  R3 = Resistor [tolerance=±5% resistance=470 package=THT]
  R4 = Resistor [tolerance=±5% resistance=470 package=THT]

nets:
  N1: Arduino1.GND, S1.Pin_1, S1.Pin_2, R2.Pin_0, R3.Pin_0, R4.Pin_0
  N2: Arduino1.D8, S1.Pin_3, S1.Pin_4, R1.Pin_1
  N3: Arduino1.D4, LED2.anode
  N4: Arduino1.D3, LED1.anode
  N5: Arduino1.D2, LED3.anode
  N6: Arduino1.+5V, R1.Pin_0
  N7: LED1.cathode, R2.Pin_1
  N8: LED2.cathode, R3.Pin_1
  N9: LED3.cathode, R4.Pin_1
